# Fritzing sketch Robotic Arm (saved by Fritzing 0.8.7b)
circuit board: 4.68405cm x 6.5cm
breadboards: 1

parts:
  D11 = female pin header, 3 pins [form="♀ (female)"]
  D10 = female pin header, 3 pins [form="♀ (female)"]
  D09 = female pin header, 3 pins [form="♀ (female)"]
  D06 = female pin header, 3 pins [form="♀ (female)"]
  D05 = female pin header, 3 pins [form="♀ (female)"]
  D03 = female pin header, 3 pins [form="♀ (female)"]
  Nano = Arduino Nano (Rev3.0)
  SW = female pin header, 2 pins [form="♀ (female)"]
  VCC = female pin header, 2 pins [form="♀ (female)"]
  5V_GND_TX_RX = Generic female header - 4 pins [form="♀ (female)" package=THT]
  5V_Servo = female pin header, 2 pins [form="♀ (female)"]
  SW1 = female pin header, 2 pins [form="♀ (female)"]
  PCA9685 = PCA9685 16x12-bit PWM Breakout

nets:
  N1: D11.pin1, Nano.D11/MOSI
  N2: D11.pin2, D10.pin2, D09.pin2, D06.pin2, D05.pin2, D03.pin2, SW1.pin1, PCA9685.no_name_yet#106, PCA9685.no_name_yet#506
  GND: D11.pin3, D10.pin3, D09.pin3, D06.pin3, D05.pin3, D03.pin3, Nano.GND, VCC.pin2, 5V_GND_TX_RX.GND, 5V_Servo.pin2, PCA9685.no_name_yet#501, PCA9685.no_name_yet#1007
  N3: D10.pin1, Nano.D10
  N4: D09.pin1, Nano.D9
  N5: D06.pin1, Nano.D6
  N6: D05.pin1, Nano.D5
  N7: D03.pin1, Nano.D3
  N8: Nano.D7, 5V_GND_TX_RX.RXD
  N9: Nano.D8, 5V_GND_TX_RX.TXD
  VIN: Nano.VIN, SW.pin1, 5V_GND_TX_RX.VCC, PCA9685.no_name_yet#505
  N10: Nano.A5, PCA9685.no_name_yet#503
  N11: Nano.A4, PCA9685.no_name_yet#504
  N12: SW.pin2, VCC.pin1
  N13: 5V_Servo.pin1, SW1.pin2

notes:
  [6-DoF] Robotic Arm (Arduino Based)

custom parts:
  Generic female header - 4 pins: Generic female header
